# Fritzing sketch WSN (saved by Fritzing 0.9.3b)
breadboards: 1

parts:
  U1 = atmega328 [package=dip]
  5V = 4 x AAA Battery Mount
  XTAL1 = Crystal [frequency="16 Mhz" package=THT]
  22_pF = Capacitor [package=cap-pth-small]
  22_pF_2 = Capacitor [package=cap-pth-small]
  S1 = Round Pushbutton
  R1 = Resistor [tolerance=±5% resistance=470 package="0805 [SMD]"]
  Power_Indicator = LED - 5mm [color="Red (633nm)" package="5 mm [THT]"]
  T1 = LM35 Temperature Sensor [package="TO92 [THT]"]
  Smoke_Detector = MQ-7 breakout
  Flame_Sensor = KY-026
  R2 = Resistor [tolerance=±5% resistance=1k package=THT]
  R3 = Resistor [tolerance=±5% resistance=2.2k package=THT]
  RESET = Pushbutton [package=THT]
  R4 = Resistor [tolerance=±5% resistance=1k package=THT]
  Espessif_Serial_Wifi_Modul_1 = ESP8266 ESP01 [part_number=ESP8266 package=THT]

nets:
  N1: U1.RESET, RESET.leg1, R4.Pin_1
  N2: U1.D0_(RX), Espessif_Serial_Wifi_Modul_1.TXD
  N3: U1.D1_(TX), Espessif_Serial_Wifi_Modul_1.RXD
  VCC: U1.VCC, U1.AVCC, S1.leg1, R1.Pin_1, T1.+Vs, Smoke_Detector.VCC, Flame_Sensor.pin3, R2.Pin_1, RESET.leg0
  GND: U1.GND, 5V.-, 22_pF.2, 22_pF_2.2, Power_Indicator.cathode, T1.GND, Smoke_Detector.GND, Flame_Sensor.pin2, R3.Pin_0, R4.Pin_0, Espessif_Serial_Wifi_Modul_1.GND
  N4: U1.XLAT1, XTAL1.pin_0, 22_pF.1
  N5: U1.XLAT2, XTAL1.pin_1, 22_pF_2.1
  N6: U1.D11_(PWM), Flame_Sensor.pin4
  N7: U1.D12, Smoke_Detector.DO
  N8: U1.A0, T1.Vout
  N9: U1.A1, Smoke_Detector.AO
  N10: U1.A2, Flame_Sensor.pin1
  N11: 5V.+, S1.leg0
  N12: R1.Pin_0, Power_Indicator.anode
  N13: R2.Pin_0, R3.Pin_1, Espessif_Serial_Wifi_Modul_1.VCC, Espessif_Serial_Wifi_Modul_1.CH_PD

custom parts:
  MQ-7 breakout: SKU: 101282
  KY-026: ky-026 flame sensor module
  ESP8266 ESP01: Generic WiFi Module based on the ESP8266 with onboard PCB antenna and UART communications
