# Fritzing sketch WristWatch (saved by Fritzing 0.9.3b)
breadboards: 1

parts:
  5V = 4 x AAA Battery Mount
  XTAL1 = Crystal [frequency="16 Mhz" package=THT]
  22_pF = Capacitor [package=cap-pth-small]
  22_pF_2 = Capacitor [package=cap-pth-small]
  S1 = Round Pushbutton
  R1 = Resistor [tolerance=±5% resistance=470 package="0805 [SMD]"]
  Power_Indicator = LED - 5mm [color="Red (633nm)" package="5 mm [THT]"]
  RESET = Pushbutton [package=THT]
  R4 = Resistor [tolerance=±5% resistance=1k package=THT]
  OLED_Display = Module display OLED I2C 128x64 SSD1306 [package=THT]
  Espessif_Serial_Wifi_Modul_1 = ESP8266 ESP01 [part_number=ESP8266 package=THT]
  R5 = Resistor [tolerance=±5% resistance=2.2k package=THT]
  R6 = Resistor [tolerance=±5% resistance=1k package=THT]
  U1 = atmega328 [package=dip]

nets:
  GND: 5V.-, 22_pF.2, 22_pF_2.2, Power_Indicator.cathode, R4.Pin_0, OLED_Display.GND, Espessif_Serial_Wifi_Modul_1.GND, R5.Pin_0, U1.GND
  N1: 5V.+, S1.leg0
  N2: XTAL1.pin_0, 22_pF.1, U1.XLAT1
  N3: XTAL1.pin_1, 22_pF_2.1, U1.XLAT2
  VCC: S1.leg1, R1.Pin_1, RESET.leg0, OLED_Display.VCC, R6.Pin_1, U1.VCC, U1.AVCC
  N4: R1.Pin_0, Power_Indicator.anode
  N5: RESET.leg1, R4.Pin_1, U1.RESET
  N6: OLED_Display.SCL, U1.A0
  N7: OLED_Display.SDA, U1.A1
  N8: Espessif_Serial_Wifi_Modul_1.RXD, U1.D1_(TX)
  N9: Espessif_Serial_Wifi_Modul_1.TXD, U1.D0_(RX)
  N10: Espessif_Serial_Wifi_Modul_1.VCC, Espessif_Serial_Wifi_Modul_1.CH_PD, R5.Pin_1, R6.Pin_0

custom parts:
  Module display OLED I2C 128x64 SSD1306: Ecran OLED I2C SSD163 de 128x64 avec connexion I2C
  ESP8266 ESP01: Generic WiFi Module based on the ESP8266 with onboard PCB antenna and UART communications
